# Fritzing sketch Untitled Sketch (saved by Fritzing 0.9.3b)
breadboards: 1

parts:
  Parça1 = Arduino Uno (Rev3)
  LCD1 = LCD screen
  Parça2 = Gas Sensor Breakout Board
  LED2 = smd LED [color="Blue (525nm)" package="0603 [SMD]"]
  BAT1 = BC9VPC [package=bc9vpc]
  R4 = Trimmer Potentiometer [maximum_resistance=10kΩ package=THT]
  R5 = Resistor [tolerance=±5% resistance=220 package=THT]
  KY-1 = Keyes Relay [package=THT]
  F1 = Fan - Ventilador [package=THT]

nets:
  N1: Parça1.A0, Parça2.A1
  N2: Parça1.D12/MISO, LCD1.E
  N3: Parça1.D13/SCK, LCD1.RS
  N4: Parça1.D2, LED2.anode
  N5: Parça1.D3_PWM, LCD1.DB7
  N6: Parça1.D4, LCD1.DB6
  N7: Parça1.D5_PWM, LCD1.DB5
  N8: Parça1.D6_PWM, LCD1.DB4
  N9: Parça1.D7, KY-1.signal
  GND: LCD1.VSS, LCD1.R/W, LCD1.LED-, Parça2.GND, LED2.cathode, BAT1.V-, R4.leg2, KY-1.ground, F1.GND
  N10: LCD1.VDD, BAT1.V+, R4.leg1, R5.Pin_1, KY-1.power, KY-1.C
  N11: LCD1.V0, R4.wiper
  N12: LCD1.LED+, R5.Pin_0
  N13: KY-1.NO, F1.5V

custom parts:
  Keyes Relay: The Keyes 5V relay module is suitable for SCM development, home appliance control. It uses a 5V~12V TIL control signal which can control DC / AC signal.
  Fan - Ventilador: Ventilador de 2 pines, se encuentra comunmente en computadoras de escritorio

// code stored in the sketch: Untitled2.ino

#include <SoftwareSerial.h>


#include <LiquidCrystal.h>



LiquidCrystal lcd(13, 12, 6, 5, 4, 3); 





float t=0;

char data = 0;

int maviled=2;

int role=7;  





void setup() 



{   

               



  Serial.begin(9600); 



  pinMode(role,OUTPUT);  

  pinMode(maviled,OUTPUT);

  

  

  lcd.begin(16, 2);  





  lcd.setCursor(0,0); 



  lcd.print("     HOS");



  lcd.setCursor(0,1);



  lcd.print("   GELDINIZ        "); 



  delay(3000);





  lcd.clear();



  lcd.setCursor(0,0);



  lcd.print("     HAVA"); 



  lcd.setCursor(0,1);



  lcd.print("KALITE MONITORU");  



  

 }









void loop()



{



  delay(1000);



  t = analogRead(A0);  

  Serial.print("Airquality = ");



  Serial.println(t);



  lcd.clear();

  lcd.setCursor (0, 0);

  lcd.print ("Hava Kal.: ");

  lcd.print (t);

  lcd.print (" PPM ");

  

  lcd.setCursor (0,1);

  if (t<=500)

   {

   lcd.print("Temiz Hava");

   Serial.print("Temiz Hava ");

   digitalWrite(maviled,LOW);

   digitalWrite(role,LOW);  

}

  else

{

   lcd.print("Kirli Hava");

   Serial.print("Kirli Hava");

   digitalWrite(maviled,HIGH);

   digitalWrite(role,HIGH);  

  

}

  

 





}
